# Fritzing sketch medidor_humedad_temperatura (saved by Fritzing 0.9.4)
breadboards: 1

parts:
  LED1 = smd LED [color="Red (633nm)" package="1206 [SMD]"]
  LED2 = smd LED [color="Yellow (585nm)" package="1206 [SMD]"]
  LED3 = smd LED [color="Green (555nm)" package="1206 [SMD]"]
  Componente1 = Arduino Uno (Rev3)
  J1 = DHT22 temperature-humidity sensor [form="♂ (male)" package=THT]
  Display1 = LCD screen 16x2 IIC [part_number=101290]

nets:
  GND: LED1.cathode, LED2.cathode, LED3.cathode, Componente1.GND, J1.GND, Display1.GND
  N1: LED1.anode, Componente1.D4
  N2: LED2.anode, Componente1.D5_PWM
  N3: LED3.anode, Componente1.D3_PWM
  N4: Componente1.A4/SDA, Display1.SDA
  N5: Componente1.A5/SCL, Display1.SCL
  N6: Componente1.D2, J1.OUT
  VCC: Componente1.5V, J1.VCC, Display1.VCC

custom parts:
  DHT22 temperature-humidity sensor: The DHT22 is a basic, low-cost digital temperature and humidity sensor. It uses a capacitive humidity sensor and a thermistor to measure the surrounding air, and spits out a digital signal on the data pin (no analog input pins needed). It's fairly simple to use, but requires careful timing to grab data. The only real downside of this sensor is you can only get new data from it once every 2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
  LCD screen 16x2 IIC: LCD screen with HD44780 controller enables showing text, symbols, value or anything else that comes from Croduino/Arduino. It is capable of showing 16 symbols in two lines and therefore can be used in many projects that need to send clearly visible and legible output information.. • Color of symbols: White • Backlight: Blue • Dimensions: 80 x 36 x 12 mm • Screen dimensions: 64.5 x 16 mm •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

// code stored in the sketch: medidor_temperatura_humedad.ino
#define DHTPIN 2     // pin usado para recibir la medición
#define DHTTYPE DHT22   // impirtante verificar que sea el sensor que estamos usando
 
// Inicializamos el sensor DHT11
DHT dht(DHTPIN, DHTTYPE);

//Declaro las variables
int BuenaH = 3; //Led verde
int AltaH = 4; //Led Rojo
int BajaH = 5; //Led Amarillo

void setup() {
  // put your setup code here, to run once:
  //Asignamos el led como una salida
  //pinMode solo se utiliza para pines digitales
  pinMode(BuenaH,OUTPUT); 
  pinMode(AltaH,OUTPUT);
  pinMode(BajaH,OUTPUT);
  
  // Inicializamos comunicación serie
  Serial.begin(9600);
 
  // Inicializamos el sensor DHT
  dht.begin();

  // Inicializamos el LCD,
  lcd.begin();
  lcd.setBacklight(HIGH);

}

void loop() {
  // put your main code here, to run repeatedly:
  // Esperamos 2 segundos entre cada medida del sensor
  delay(2000);
 
  // Leemos la humedad relativa
  float h = dht.readHumidity();
  // Leemos la temperatura en grados centígrados (por defecto)
  float t = dht.readTemperature();
 
  // Comprobamos si ha habido algún error en la lectura
  if (isnan(h) || isnan(t)) {
    Serial.println("Error obteniendo los datos del sensor DHT11");
    return;
  }

  //mensajes LCD
  lcd.clear(); // limpiamos LCD
  
  lcd.setCursor (0, 0); // vamos al inicio de la linea 1
  lcd.print("Humedad: ");
  lcd.print(h);
  
  lcd.setCursor (0, 1); // vamos al inicio de la linea 2
  lcd.print("Temp: ");
  lcd.print(t);
  
  //mensajes Serial 
  Serial.println("Humedad: ");
  Serial.println(h);
  Serial.print(" %\t");
  Serial.println("Temperatura: ");
  Serial.println(t);
  Serial.print(" *C ");

  //Para saber si la humedad se encuentra en rangos optimos
  //Prendemos los leds
  if((h >= 60) && (h<=70)) {
    //Buena humedad
    //Prende led verde
    digitalWrite(BuenaH, HIGH);
    digitalWrite(AltaH, LOW);
    digitalWrite(BajaH, LOW);
  }

  else if (h > 70) {
    //Alta humedad
    //Prende led rojo
    digitalWrite(BuenaH, LOW);
    digitalWrite(AltaH, HIGH);
    digitalWrite(BajaH, LOW);
  }
    
  else {
    //baja humedad
    //Prende led amarillo
   digitalWrite(BuenaH, LOW);
    digitalWrite(AltaH, LOW);
    digitalWrite(BajaH, HIGH);
  }
    
}
